// Logisim project Address Mapper.circ as structural Verilog: 1 circuit, main circuit Address Mapper
module Address_Mapper (
  input  [15:0] Map,
  input  [15:0] Mask,
  input  [15:0] Address,
  input  WE_In,
  input  RE_In,
  output WE_Out,
  output RE_Out
);

  wire comparator_1_eq;
  wire [15:0] and_1_out;

  Comparator #(.mode("unsigned"), .width(16)) comparator_1 (
    .a(Map), .b(and_1_out), .eq(comparator_1_eq));  // open: gt, lt
  assign and_1_out = Mask & Address;  // AND_Gate and_1, 16 bits wide
  and and_2 (WE_Out, comparator_1_eq, WE_In);
  and and_3 (RE_Out, comparator_1_eq, RE_In);
endmodule
