// Logisim project Carry Look Ahead Adder.circ as structural Verilog: 2 circuits, main circuit main
module PGAdder (
  input  Cin,
  input  A,
  input  B,
  output P,
  output G,
  output Sum
);

  wire nand_1_out, nand_2_out, nand_3_out, nand_4_out, not_1_out, not_2_out, not_3_out;

  not not_1 (not_1_out, A);
  not not_2 (not_2_out, B);
  not not_3 (not_3_out, Cin);
  xor xor_1 (P, A, B);
  and and_1 (G, A, B);
  nand nand_1 (nand_1_out, not_3_out, not_2_out, A);
  nand nand_2 (nand_2_out, not_3_out, B, not_1_out);
  nand nand_3 (nand_3_out, Cin, not_2_out, not_1_out);
  nand nand_4 (nand_4_out, Cin, B, A);
  nand nand_5 (Sum, nand_1_out, nand_2_out, nand_3_out, nand_4_out);
endmodule

module PGBlock (
  input  Pl,
  input  Ph,
  input  Gl,
  input  Gh,
  input  Cin,
  output P,
  output G,
  output Cl,
  output Ch
);

  wire and_2_out, and_3_out;

  and and_1 (P, Pl, Ph);
  and and_2 (and_2_out, Ph, Gl);
  and and_3 (and_3_out, Pl, Cin);
  or or_1 (G, and_2_out, Gh);
  or or_2 (Ch, Gl, and_3_out);

  assign Cl = Cin;
endmodule
