// Logisim project Hamming Error Corrector.circ as structural Verilog: 2 circuits, main circuit Hamming Generator
module Hamming_Generator (
  input  D1in,
  input  D2in,
  input  D3in,
  input  D4in,
  output p1,
  output p2,
  output D1out,
  output p3,
  output D2out,
  output D3out,
  output D4out
);

  wire xor_1_out, xor_3_out, xor_5_out;

  xor xor_1 (xor_1_out, D1in, D2in);
  xor xor_2 (p1, xor_1_out, D4in);
  xor xor_3 (xor_3_out, D1in, D3in);
  xor xor_4 (p2, xor_3_out, D4in);
  xor xor_5 (xor_5_out, D2in, D3in);
  xor xor_6 (p3, xor_5_out, D4in);

  assign D1out = D1in;
  assign D2out = D2in;
  assign D3out = D3in;
  assign D4out = D4in;
endmodule

module Hamming_Corrector (
  input  D1in,
  input  D2in,
  input  D3in,
  input  D4in,
  input  p1,
  input  p2,
  input  p3,
  output D1out,
  output D2out,
  output D3out,
  output D4out
);

  wire and_1_out, and_2_out, and_3_out, and_4_out;

  and and_1 (and_1_out, p1, p2, ~p3);  // AND_Gate
  and and_2 (and_2_out, p1, ~p2, p3);  // AND_Gate
  and and_3 (and_3_out, ~p1, p2, p3);  // AND_Gate
  and and_4 (and_4_out, p1, p2, p3);
  xor xor_1 (D1out, D1in, and_1_out);
  xor xor_2 (D2out, D2in, and_2_out);
  xor xor_3 (D3out, D3in, and_3_out);
  xor xor_4 (D4out, D4in, and_4_out);
endmodule
